# Fritzing sketch fritzing (saved by Fritzing 0.9.4)
breadboards: 1

parts:
  Raspberry_Pi_1 = Raspberry Pi 3 [part_number=RPI-3-V1.2]
  LED1 = smd LED [color="Green (560nm)" package="0603 [SMD]"]
  LED2 = smd LED [color="Yellow (585nm)" package="0603 [SMD]"]
  LED3 = smd LED [color="Green (560nm)" package="0603 [SMD]"]
  R4 = Resistor [tolerance=±5% resistance=220 package="0402 [SMD]"]
  R5 = Resistor [tolerance=±5% resistance=220 package="0402 [SMD]"]
  R6 = Resistor [tolerance=±5% resistance=220 package="0402 [SMD]"]

nets:
  N1: Raspberry_Pi_1.GND, LED1.cathode, LED2.cathode, LED3.cathode
  N2: Raspberry_Pi_1.GPIO21, R6.Pin_1
  N3: Raspberry_Pi_1.GPIO20, R4.Pin_1
  N4: Raspberry_Pi_1.GPIO16, R5.Pin_1
  N5: LED1.anode, R5.Pin_0
  N6: LED2.anode, R4.Pin_0
  N7: LED3.anode, R6.Pin_0
